// Logisim project MIPS32.circ as structural Verilog
module MIPS32 (
);

  wire and_1_out, and_2_out, and_3_out, c1_out, Choose2, maincontrol_1_signextend, or_1_out, Q, RegWrite;
  wire [1:0] Choose10, EXCtrl_q, maincontrol_1_memtoreg, maincontrol_1_regdest, PC_q, WBCtrl0_q_2, WBCtrl1_q,
       WBCtrl2_q;
  wire [1:1] WBCtrl0_q;
  wire [2:0] maincontrol_1_memread, MEMCtrl0_q;
  wire [3:0] ALUOP;
  wire [4:0] Dest0_q, multiplexer_3_out, Rd_q, RegDest, Rt_q, SA;
  wire [29:0] incrementer_1_p2, PC_q_2;
  wire [31:0] A_q, ALUresult1_q, ALUresultD_q, B_q, bit_extender_1_out, bit_extender_2_out, Imm_q,
       Instruction_q, lui_1_outp, MEMdata_q, mips_alu_1_p5, mipsprogramrom_1_p2, movz_1_outp,
       multiplexer_1_out, multiplexer_2_out, multiplexer_5_out, PC4DE_q, PC4EM_q, PC4FD_q, registerfile_1_p6,
       registerfile_1_p7, WBdata;

  Clock c1 (.out(c1_out));
  Register #(.width(32), .trigger("falling")) PC (
    .D({incrementer_1_p2, PC_q}), .clk(c1_out), .Q({PC_q_2, PC_q}));  // open: en, clr
  // Incrementer #(.width(30)) incrementer_1: pin names not known; wires that end beside it: PC_q_2, incrementer_1_p2
  // MIPSProgramROM mipsprogramrom_1: pin names not known; wires that end beside it: {PC_q_2, PC_q}, mipsprogramrom_1_p2
  Register #(.width(32), .trigger("falling")) PC4FD (
    .D({incrementer_1_p2, PC_q}), .clk(c1_out), .Q(PC4FD_q));  // open: en, clr
  Register #(.width(32), .trigger("falling")) Instruction (
    .D(mipsprogramrom_1_p2), .clk(c1_out), .Q(Instruction_q));  // open: en, clr
  // RegisterFile registerfile_1: pin names not known; wires that end beside it: WBdata, RegWrite, RegDest, Instruction_q[25:21], Instruction_q[20:16], registerfile_1_p6, registerfile_1_p7
  assign bit_extender_1_out = {{16{1'b0}}, Instruction_q[15:0]};  // Bit_Extender bit_extender_1
  Multiplexer #(.width(32), .enable("false")) multiplexer_1 (
    .in0(bit_extender_1_out), .in1(bit_extender_2_out), .out(multiplexer_1_out),
    .sel(maincontrol_1_signextend));
  assign bit_extender_2_out = {{16{Instruction_q[15]}}, Instruction_q[15:0]};  // Bit_Extender bit_extender_2
  MainControl maincontrol_1 (
    .OP5(Instruction_q[31]), .OP4(Instruction_q[30]), .OP3(Instruction_q[29]), .OP2(Instruction_q[28]),
    .OP1(Instruction_q[27]), .OP0(Instruction_q[26]), .SignExtend(maincontrol_1_signextend),
    .RegDest(maincontrol_1_regdest[0]), .ALUsrc(maincontrol_1_regdest[1]),
    .MemRead(maincontrol_1_memread[0]), .MemW(maincontrol_1_memread[1]), .Branch(maincontrol_1_memread[2]),
    .MemToReg(maincontrol_1_memtoreg[0]), .RegWr(maincontrol_1_memtoreg[1]));
  Register #(.width(32), .trigger("falling")) PC4DE (.D(PC4FD_q), .clk(c1_out), .Q(PC4DE_q));  // open: en, clr
  Register #(.width(32), .trigger("falling")) A (.D(registerfile_1_p6), .clk(c1_out), .Q(A_q));  // open: en, clr
  Register #(.width(32), .trigger("falling")) B (.D(registerfile_1_p7), .clk(c1_out), .Q(B_q));  // open: en, clr
  Register #(.width(32), .trigger("falling")) Imm (.D(multiplexer_1_out), .clk(c1_out), .Q(Imm_q));  // open: en, clr
  Register #(.width(5), .trigger("falling")) Rd (.D(Instruction_q[15:11]), .clk(c1_out), .Q(Rd_q));  // open: en, clr
  Register #(.width(5), .trigger("falling")) Rt (.D(Instruction_q[20:16]), .clk(c1_out), .Q(Rt_q));  // open: en, clr
  Register #(.width(2), .trigger("falling")) EXCtrl (
    .D(maincontrol_1_regdest), .clk(c1_out), .Q(EXCtrl_q));  // open: en, clr
  Register #(.width(3), .trigger("falling")) MEMCtrl0 (
    .D(maincontrol_1_memread), .clk(c1_out), .Q(MEMCtrl0_q));  // open: en, clr
  Register #(.width(2), .trigger("falling")) WBCtrl0 (
    .D(maincontrol_1_memtoreg), .clk(c1_out), .Q({WBCtrl0_q[1], WBCtrl0_q_2[0]}));  // open: en, clr
  Multiplexer #(.width(32), .enable("false")) multiplexer_2 (
    .in0(B_q), .in1(Imm_q), .out(multiplexer_2_out), .sel(EXCtrl_q[1]));
  Multiplexer #(.width(5), .enable("false")) multiplexer_3 (
    .in0(Rd_q), .in1(Rt_q), .out(multiplexer_3_out), .sel(EXCtrl_q[0]));
  // Mips_ALU mips_alu_1: pin names not known; wires that end beside it: A_q, multiplexer_2_out, ALUOP, SA, mips_alu_1_p5
  and and_1 (and_1_out, ~Choose2, Q);  // AND_Gate
  and and_2 (and_2_out, ~Q, Choose2);  // AND_Gate
  and and_3 (and_3_out, Choose10[0], Choose10[1]);
  LUI lui_1 (.B(multiplexer_2_out), .Outp(lui_1_outp));
  MOVZ movz_1 (.rt(Rt_q), .rs_A(A_q), .Outp(movz_1_outp), .RegWr_Q(Q));
  or or_1 (or_1_out, and_1_out, and_2_out);
  Multiplexer #(.enable("false")) multiplexer_4 (
    .in0(WBCtrl0_q[1]), .in1(or_1_out), .out(WBCtrl0_q_2[1]), .sel(and_3_out));
  Multiplexer #(.select(2), .width(32), .enable("false")) multiplexer_5 (
    .in0(mips_alu_1_p5), .in1(lui_1_outp), .in2(movz_1_outp), .out(multiplexer_5_out), .sel(Choose10));  // open: in3
  Register #(.width(32), .trigger("falling")) PC4EM (.D(PC4DE_q), .clk(c1_out), .Q(PC4EM_q));  // open: en, clr
  Register #(.width(32), .trigger("falling")) ALUresultD (
    .D(multiplexer_5_out), .clk(c1_out), .Q(ALUresultD_q));  // open: en, clr
  Register #(.width(32), .trigger("falling")) Bdata (.D(B_q));  // open: en, clk, Q, clr
  Register #(.width(5), .trigger("falling")) Dest0 (.D(multiplexer_3_out), .clk(c1_out), .Q(Dest0_q));  // open: en, clr
  Register #(.width(3), .trigger("falling")) MEMCtrl1 (.D(MEMCtrl0_q), .clk(c1_out));  // open: en, Q, clr
  Register #(.width(2), .trigger("falling")) WBCtrl1 (.D(WBCtrl0_q_2), .clk(c1_out), .Q(WBCtrl1_q));  // open: en, clr
  // MIPS_RAM mips_ram_1: pin names not known
  Register #(.width(32), .trigger("falling")) PC4MW (.D(PC4EM_q), .clk(c1_out));  // open: en, Q, clr
  Register #(.width(32), .trigger("falling")) ALUresult1 (
    .D(ALUresultD_q), .clk(c1_out), .Q(ALUresult1_q));  // open: en, clr
  Register #(.width(32), .trigger("falling")) MEMdata (.clk(c1_out), .Q(MEMdata_q));  // open: D, en, clr
  Register #(.width(5), .trigger("falling")) Dest1 (.D(Dest0_q), .clk(c1_out), .Q(RegDest));  // open: en, clr
  Register #(.width(2), .trigger("falling")) WBCtrl2 (.D(WBCtrl1_q), .clk(c1_out), .Q(WBCtrl2_q));  // open: en, clr
  Multiplexer #(.width(32), .enable("false")) multiplexer_6 (
    .in0(ALUresult1_q), .in1(MEMdata_q), .out(WBdata));  // open: sel

  // Notes on the sheet:
  //   IF stage
  //   contents of mipsprogramrom_1 (hex, n*v repeats v):
  //   ADDIU $1,$10,-1001 ANDI $10,$10,1001 ORI $10,$10,1001 XORI $10,$10,1001
  //   ID stage
  //   EX stage
  //   MEM stage
  //   WB stage
endmodule

module MainControl (
  input  OP5,
  input  OP4,
  input  OP3,
  input  OP2,
  input  OP1,
  input  OP0,
  output SignExtend,
  output RegDest,
  output ALUsrc,
  output MemRead,
  output MemW,
  output Branch,
  output MemToReg,
  output RegWr
);

  wire and_5_out, and_6_out, and_7_out, not_2_out, not_3_out, not_4_out, not_5_out, not_6_out, not_7_out,
       not_8_out, not_9_out, not_10_out;

  not not_1 (SignExtend, OP2);
  not not_2 (not_2_out, OP5);
  not not_3 (not_3_out, OP3);
  or or_1 (ALUsrc, OP3, OP5);
  not not_4 (not_4_out, OP3);
  and and_1 (MemW, OP5, OP3);
  not not_5 (not_5_out, OP5);
  not not_6 (not_6_out, OP3);
  not not_7 (not_7_out, OP3);
  not not_8 (not_8_out, OP2);
  not not_9 (not_9_out, OP5);
  not not_10 (not_10_out, OP3);
  and and_2 (RegDest, not_2_out, not_3_out);
  and and_3 (MemRead, OP5, not_4_out);
  and and_4 (Branch, not_5_out, not_6_out, OP2);
  and and_5 (and_5_out, not_7_out, not_8_out);
  and and_6 (and_6_out, not_9_out, OP3);
  and and_7 (and_7_out, OP5, not_10_out);
  or or_2 (RegWr, and_5_out, and_6_out, and_7_out);

  assign MemToReg = OP5;
endmodule

module LUI (
  input  [31:0] B,
  output [31:0] Outp
);


  assign Outp = {B[15:0], B[31:16]};
endmodule

module MOVZ (
  input  [4:0] rt,
  input  [31:0] rs_A,
  output [31:0] Outp,
  output RegWr_Q
);

  wire [4:0] not_1_out;

  assign not_1_out = ~rt;  // NOT_Gate not_1, 5 bits wide
  and and_1 (RegWr_Q, not_1_out[0], not_1_out[1], not_1_out[2], not_1_out[3], not_1_out[4]);

  assign Outp = rs_A;
endmodule
